// Logisim project lab8.circ as structural Verilog: 2 circuits, main circuit main
module main (
  input  [3:0] in_1,
  input  [3:0] in_2,
  input  [3:0] in_3,
  input  [3:0] in_4,
  input  Carry_In,
  input  Carry_In_2,
  output [4:0] out_7,
  output [4:0] out_8
);

  wire and_1_out, and_2_out, and_3_out, and_4_out, and_5_out, and_6_out, and_7_out, and_8_out,
       full_adder_1_c, full_adder_2_c, full_adder_3_c, or_1_out, or_2_out, or_3_out, xor_1_out, xor_2_out,
       xor_3_out, xor_4_out;

  xor xor_1 (xor_1_out, in_2[0], in_4[0]);
  and and_1 (and_1_out, in_2[0], in_4[0]);
  xor xor_2 (xor_2_out, in_2[1], in_4[1]);
  and and_2 (and_2_out, in_2[1], in_4[1]);
  xor xor_3 (xor_3_out, in_2[2], in_4[2]);
  and and_3 (and_3_out, in_2[2], in_4[2]);
  xor xor_4 (xor_4_out, in_2[3], in_4[3]);
  and and_4 (and_4_out, in_2[3], in_4[3]);
  xor xor_5 (out_8[0], xor_1_out, Carry_In_2);
  and and_5 (and_5_out, xor_1_out, Carry_In_2);
  xor xor_6 (out_8[1], xor_2_out, or_1_out);
  and and_6 (and_6_out, xor_2_out, or_1_out);
  xor xor_7 (out_8[2], xor_3_out, or_2_out);
  and and_7 (and_7_out, xor_3_out, or_2_out);
  xor xor_8 (out_8[3], xor_4_out, or_3_out);
  and and_8 (and_8_out, xor_4_out, or_3_out);
  or or_1 (or_1_out, and_5_out, and_1_out);
  or or_2 (or_2_out, and_6_out, and_2_out);
  or or_3 (or_3_out, and_7_out, and_3_out);
  or or_4 (out_8[4], and_8_out, and_4_out);
  Full_Adder full_adder_1 (.X(in_1[0]), .Y(in_3[0]), .Z(Carry_In), .S(out_7[0]), .C(full_adder_1_c));
  Full_Adder full_adder_2 (.X(in_1[1]), .Y(in_3[1]), .Z(full_adder_1_c), .S(out_7[1]), .C(full_adder_2_c));
  Full_Adder full_adder_3 (.X(in_1[2]), .Y(in_3[2]), .Z(full_adder_2_c), .S(out_7[2]), .C(full_adder_3_c));
  Full_Adder full_adder_4 (.X(in_1[3]), .Y(in_3[3]), .Z(full_adder_3_c), .S(out_7[3]), .C(out_7[4]));

  // Notes on the sheet:
  //   X (4bit Input)
  //   Y (4bit Input)
  //   S
  //   C
  //   S
  //   C
  //   S
  //   C
  //   S
  //   C
  //   Output
  //   X (4bit Input)
  //   Y (4bit Input)
  //   Output
endmodule

module Full_Adder (
  input  X,
  input  Y,
  input  Z,
  output S,
  output C
);

  wire and_1_out, and_2_out, xor_1_out;

  xor xor_1 (xor_1_out, X, Y);
  and and_1 (and_1_out, X, Y);
  xor xor_2 (S, xor_1_out, Z);
  and and_2 (and_2_out, xor_1_out, Z);
  or or_1 (C, and_2_out, and_1_out);
endmodule
