// Logisim project lec19latches.circ as structural Verilog: 1 circuit, main circuit main
module main (
  input  in_1,
  input  in_2,
  input  in_3,
  input  in_4,
  input  in_5,
  input  in_6,
  input  Pre,
  input  in_8,
  input  in_9,
  input  in_10,
  input  in_11,
  input  in_12,
  input  in_13,
  input  in_14,
  input  Clear,
  input  in_16,
  input  in_17,
  output out_18,
  output out_19,
  output out_20,
  output out_21,
  output out_22,
  output out_23,
  output out_24,
  output out_25,
  output out_26,
  output out_27,
  output out_28,
  output out_29
);

  wire nand_1_out, nand_2_out, nand_3_out, nand_4_out, nand_8_out, nand_9_out, nand_10_out, nand_11_out,
       not_1_out, not_2_out, not_3_out, not_4_out, not_5_out, not_6_out, not_7_out, not_8_out, not_9_out,
       not_10_out, not_11_out, not_12_out, not_13_out, not_14_out, not_15_out, not_16_out, not_17_out,
       not_18_out, not_19_out;

  not not_1 (not_1_out, in_16);
  nand nand_1 (nand_1_out, in_10, in_12);
  nand nand_2 (nand_2_out, in_12, in_14);
  nand nand_3 (nand_3_out, in_16, in_17);
  nand nand_4 (nand_4_out, in_17, not_1_out);
  // NAND_Gate nand_5 is placed but not wired
  nor nor_1 (out_18, in_2, out_20);
  nor nor_2 (out_20, out_18, in_4);
  nand nand_6 (out_22, in_6, out_23);
  nand nand_7 (out_23, out_22, in_8);
  not not_2 (not_2_out, nand_3_out);
  not not_3 (not_3_out, out_29);
  not not_4 (not_4_out, out_28);
  not not_5 (not_5_out, nand_4_out);
  not not_6 (not_6_out, nand_1_out);
  or or_1 (out_25, not_6_out, not_7_out);
  not not_7 (not_7_out, out_27);
  not not_8 (not_8_out, out_25);
  or or_2 (out_27, not_8_out, not_9_out);
  not not_9 (not_9_out, nand_2_out);
  or or_3 (out_28, not_2_out, not_3_out);
  or or_4 (out_29, not_4_out, not_5_out);
  nand nand_8 (nand_8_out, out_21, in_1, in_3);
  nand nand_9 (nand_9_out, in_3, in_5, out_19);
  nand nand_10 (nand_10_out, out_26, Clear, in_9, in_11);
  nand nand_11 (nand_11_out, in_11, in_13, Pre, out_24);
  not not_10 (not_10_out, nand_8_out);
  not not_11 (not_11_out, out_21);
  not not_12 (not_12_out, out_19);
  not not_13 (not_13_out, nand_9_out);
  not not_14 (not_14_out, Pre);
  not not_15 (not_15_out, nand_10_out);
  not not_16 (not_16_out, out_26);
  not not_17 (not_17_out, out_24);
  not not_18 (not_18_out, nand_11_out);
  not not_19 (not_19_out, Clear);
  or or_5 (out_19, not_10_out, not_11_out);
  or or_6 (out_21, not_12_out, not_13_out);
  or or_7 (out_24, not_15_out, not_14_out, not_16_out);
  or or_8 (out_26, not_17_out, not_19_out, not_18_out);

  // Notes on the sheet:
  //   S-R (Set Reset) Latch
  //   Active-Low S-R (Set Reset) Latch
  //   Gated S-R Latch
  //   Gated D-Latch
  //   J-K Flip Flop
  //   J-K Flip Flop Asynchronous
endmodule
